# Fritzing sketch IRtoLEDWireDiagram (saved by Fritzing 0.9.2b)
breadboards: 1

parts:
  Part1 = Arduino Uno (Rev3) - ICSP
  J1 = Infrared Proximity Sensor
  R1 = Resistor [tolerance=±5% resistance=220 package=THT]
  LED1 = smd LED [color="Red (633nm)" package="0603 [SMD]"]

nets:
  N1: Part1.A0, J1.Vout
  N2: Part1.D7, R1.Pin_0
  5V: Part1.5V, J1.Vcc
  GND: Part1.GND, J1.GND, LED1.cathode
  N3: R1.Pin_1, LED1.anode

notes:
  The diagram features the old proximity sensor, this works with the small IR Range Finder.
